// Logisim project 8bitDisp.circ as structural Verilog: 5 circuits, main circuit main
module main (
  input  [7:0] input8bit
);

  wire [6:0] bcd7seg_1_a, bcd7seg_1_b, bcd7seg_1_c;
  wire [9:0] bin2bcd_1_out_2;

  BIN2BCD bin2bcd_1 (.in_1(input8bit), .out_2(bin2bcd_1_out_2));
  BCD7SEG bcd7seg_1 (.in_1(bin2bcd_1_out_2), .A(bcd7seg_1_a), .B(bcd7seg_1_b), .C(bcd7seg_1_c));
  _7_Segment_Display u_7_segment_display_1 (
    .g(bcd7seg_1_a[0]), .f(bcd7seg_1_a[1]), .a(bcd7seg_1_a[6]), .b(bcd7seg_1_a[5]), .e(bcd7seg_1_a[2]),
    .d(bcd7seg_1_a[3]), .c(bcd7seg_1_a[4]));  // open: dp
  _7_Segment_Display u_7_segment_display_2 (
    .g(bcd7seg_1_b[0]), .f(bcd7seg_1_b[1]), .a(bcd7seg_1_b[6]), .b(bcd7seg_1_b[5]), .e(bcd7seg_1_b[2]),
    .d(bcd7seg_1_b[3]), .c(bcd7seg_1_b[4]));  // open: dp
  _7_Segment_Display u_7_segment_display_3 (
    .g(bcd7seg_1_c[0]), .f(bcd7seg_1_c[1]), .a(bcd7seg_1_c[6]), .b(bcd7seg_1_c[5]), .e(bcd7seg_1_c[2]),
    .d(bcd7seg_1_c[3]), .c(bcd7seg_1_c[4]));  // open: dp
endmodule

module BIN2BCD (
  input  [7:0] in_1,
  output [9:0] out_2
);

  wire C1_s0, C1_s1, C1_s2, C1_s3, C2_s0, C2_s1, C2_s2, C2_s3, C3_s0, C3_s1, C3_s2, C3_s3, C4_s0, C4_s1,
       C4_s2, C4_s3, C6_s0, C6_s1, C6_s2;

  helper C1 (.A0(in_1[5]), .A1(in_1[6]), .A2(in_1[7]), .A3(1'b0), .S0(C1_s0), .S1(C1_s1), .S2(C1_s2), .S3(C1_s3));
  helper C2 (.A0(in_1[4]), .A1(C1_s0), .A2(C1_s1), .A3(C1_s2), .S0(C2_s0), .S1(C2_s1), .S2(C2_s2), .S3(C2_s3));
  helper C3 (.A0(in_1[3]), .A1(C2_s0), .A2(C2_s1), .A3(C2_s2), .S0(C3_s0), .S1(C3_s1), .S2(C3_s2), .S3(C3_s3));
  helper C6 (.A0(C3_s3), .A1(C2_s3), .A2(C1_s3), .A3(1'b0), .S0(C6_s0), .S1(C6_s1), .S2(C6_s2), .S3(out_2[9]));
  helper C4 (.A0(in_1[2]), .A1(C3_s0), .A2(C3_s1), .A3(C3_s2), .S0(C4_s0), .S1(C4_s1), .S2(C4_s2), .S3(C4_s3));
  helper C5 (
    .A0(in_1[1]), .A1(C4_s0), .A2(C4_s1), .A3(C4_s2), .S0(out_2[1]), .S1(out_2[2]), .S2(out_2[3]),
    .S3(out_2[4]));
  helper C7 (
    .A0(C4_s3), .A1(C6_s0), .A2(C6_s1), .A3(C6_s2), .S0(out_2[5]), .S1(out_2[6]), .S2(out_2[7]), .S3(out_2[8]));

  assign out_2[0] = in_1[0];
endmodule

module helper (
  input  A0,
  input  A1,
  input  A2,
  input  A3,
  output S0,
  output S1,
  output S2,
  output S3
);

  wire and_1_out, and_2_out, and_3_out, and_4_out, and_5_out, and_6_out, and_7_out, and_8_out, and_9_out,
       and_10_out, not_1_out, not_2_out, not_3_out, not_4_out;

  not not_1 (not_1_out, A0);
  not not_2 (not_2_out, A1);
  not not_3 (not_3_out, A2);
  not not_4 (not_4_out, A3);
  and and_1 (and_1_out, not_1_out, A3);
  and and_2 (and_2_out, not_1_out, A1, A2);
  and and_3 (and_3_out, A0, not_3_out, not_4_out);
  and and_4 (and_4_out, not_1_out, A3);
  and and_5 (and_5_out, A1, not_3_out);
  and and_6 (and_6_out, A0, A1);
  and and_7 (and_7_out, not_1_out, not_2_out, A2);
  and and_8 (and_8_out, A0, A3);
  and and_9 (and_9_out, A1, A2);
  and and_10 (and_10_out, A0, A2);
  or or_1 (S0, and_1_out, and_2_out, and_3_out);
  or or_2 (S1, and_4_out, and_5_out, and_6_out);
  or or_3 (S2, and_7_out, and_8_out);
  or or_4 (S3, A3, and_9_out, and_10_out);
endmodule

module BCD7SEGMENT (
  input  B3,
  input  B2,
  input  B1,
  input  B0,
  output A,
  output B,
  output C,
  output D,
  output E,
  output F,
  output G
);

  wire and_1_out, and_2_out, and_3_out, and_4_out, and_5_out, and_6_out, and_7_out, and_8_out, and_9_out,
       and_10_out, and_11_out, and_12_out, and_13_out, and_14_out, and_15_out, and_16_out, not_1_out,
       not_2_out, not_3_out;

  not not_1 (not_1_out, B2);
  not not_2 (not_2_out, B1);
  not not_3 (not_3_out, B0);
  and and_1 (and_1_out, not_1_out, not_3_out);
  and and_2 (and_2_out, B2, B0);
  and and_3 (and_3_out, not_2_out, not_3_out);
  and and_4 (and_4_out, B1, B0);
  or or_1 (C, not_2_out, B0, B2);
  and and_5 (and_5_out, not_1_out, not_3_out);
  and and_6 (and_6_out, not_1_out, B1);
  and and_7 (and_7_out, B2, not_2_out, B0);
  and and_8 (and_8_out, B1, not_3_out);
  and and_9 (and_9_out, not_1_out, not_3_out);
  and and_10 (and_10_out, B1, not_3_out);
  and and_11 (and_11_out, not_2_out, not_3_out);
  and and_12 (and_12_out, B2, not_2_out);
  and and_13 (and_13_out, B2, not_3_out);
  and and_14 (and_14_out, not_1_out, B1);
  and and_15 (and_15_out, B2, not_2_out);
  and and_16 (and_16_out, B1, not_3_out);
  or or_2 (A, and_1_out, B1, and_2_out, B3);
  or or_3 (B, not_1_out, and_3_out, and_4_out);
  or or_4 (D, and_5_out, and_6_out, and_7_out, and_8_out, B3);
  or or_5 (E, and_9_out, and_10_out);
  or or_6 (F, and_11_out, and_12_out, and_13_out, B3);
  or or_7 (G, and_14_out, and_15_out, B3, and_16_out);
endmodule

module BCD7SEG (
  input  [9:0] in_1,
  output [6:0] A,
  output [6:0] B,
  output [6:0] C
);

  BCD7SEGMENT bcd7segment_1 (
    .B1(in_1[9]), .B0(in_1[8]), .A(A[6]), .B(A[5]), .C(A[4]), .D(A[3]), .E(A[2]), .F(A[1]), .G(A[0]));  // open: B3, B2
  BCD7SEGMENT bcd7segment_2 (
    .B3(in_1[7]), .B2(in_1[6]), .B1(in_1[5]), .B0(in_1[4]), .A(B[6]), .B(B[5]), .C(B[4]), .D(B[3]), .E(B[2]),
    .F(B[1]), .G(B[0]));
  BCD7SEGMENT bcd7segment_3 (
    .B3(in_1[3]), .B2(in_1[2]), .B1(in_1[1]), .B0(in_1[0]), .A(C[6]), .B(C[5]), .C(C[4]), .D(C[3]), .E(C[2]),
    .F(C[1]), .G(C[0]));
endmodule
