// Logisim project 8bitMem.circ as structural Verilog: 3 circuits, main circuit main
module main (
  input  [7:0] Value,
  input  [1:0] Address
);

  wire Start_out, Stop_out, Write_out;
  wire [7:0] mainmemo_1_out_6;

  Button Write (.out(Write_out));
  Button Start (.out(Start_out));
  Button Stop (.out(Stop_out));
  mainMemo mainmemo_1 (
    .Value(Value), .Adress(Address), .Write(Write_out), .Beginn(Start_out), .Stopp(Stop_out),
    .out_6(mainmemo_1_out_6));
  LED led_1 (.in(mainmemo_1_out_6[0]));
  LED led_2 (.in(mainmemo_1_out_6[1]));
  LED led_3 (.in(mainmemo_1_out_6[2]));
  LED led_4 (.in(mainmemo_1_out_6[3]));
  LED led_5 (.in(mainmemo_1_out_6[4]));
  LED led_6 (.in(mainmemo_1_out_6[5]));
  LED led_7 (.in(mainmemo_1_out_6[6]));
  LED led_8 (.in(mainmemo_1_out_6[7]));
endmodule

module memory (
  input  [7:0] in_1,
  input  in_2,
  output [7:0] out_3
);

  wire demultiplexer_1_out0, demultiplexer_1_out1, demultiplexer_2_out0, demultiplexer_2_out1,
       demultiplexer_3_out0, demultiplexer_3_out1, demultiplexer_4_out0, demultiplexer_4_out1,
       demultiplexer_5_out0, demultiplexer_5_out1, demultiplexer_6_out0, demultiplexer_6_out1,
       demultiplexer_7_out0, demultiplexer_7_out1, demultiplexer_8_out0, demultiplexer_8_out1;

  Demultiplexer demultiplexer_1 (.out0(demultiplexer_1_out0), .out1(demultiplexer_1_out1), .in(1'b1), .sel(in_1[0]));
  S_R_Flip_Flop s_r_ff_1 (
    .S(demultiplexer_1_out1), .R(demultiplexer_1_out0), .clk(in_2), .Q(out_3[0]));  // open: reset, Qn, preset
  Demultiplexer demultiplexer_2 (.out0(demultiplexer_2_out0), .out1(demultiplexer_2_out1), .in(1'b1), .sel(in_1[1]));
  S_R_Flip_Flop s_r_ff_2 (
    .S(demultiplexer_2_out1), .R(demultiplexer_2_out0), .clk(in_2), .Q(out_3[1]));  // open: reset, Qn, preset
  Demultiplexer demultiplexer_3 (.out0(demultiplexer_3_out0), .out1(demultiplexer_3_out1), .in(1'b1), .sel(in_1[2]));
  S_R_Flip_Flop s_r_ff_3 (
    .S(demultiplexer_3_out1), .R(demultiplexer_3_out0), .clk(in_2), .Q(out_3[2]));  // open: reset, Qn, preset
  Demultiplexer demultiplexer_4 (.out0(demultiplexer_4_out0), .out1(demultiplexer_4_out1), .in(1'b1), .sel(in_1[3]));
  S_R_Flip_Flop s_r_ff_4 (
    .S(demultiplexer_4_out1), .R(demultiplexer_4_out0), .clk(in_2), .Q(out_3[3]));  // open: reset, Qn, preset
  Demultiplexer demultiplexer_5 (.out0(demultiplexer_5_out0), .out1(demultiplexer_5_out1), .in(1'b1), .sel(in_1[4]));
  S_R_Flip_Flop s_r_ff_5 (
    .S(demultiplexer_5_out1), .R(demultiplexer_5_out0), .clk(in_2), .Q(out_3[4]));  // open: reset, Qn, preset
  Demultiplexer demultiplexer_6 (.out0(demultiplexer_6_out0), .out1(demultiplexer_6_out1), .in(1'b1), .sel(in_1[5]));
  S_R_Flip_Flop s_r_ff_6 (
    .S(demultiplexer_6_out1), .R(demultiplexer_6_out0), .clk(in_2), .Q(out_3[5]));  // open: reset, Qn, preset
  Demultiplexer demultiplexer_7 (.out0(demultiplexer_7_out0), .out1(demultiplexer_7_out1), .in(1'b1), .sel(in_1[6]));
  S_R_Flip_Flop s_r_ff_7 (
    .S(demultiplexer_7_out1), .R(demultiplexer_7_out0), .clk(in_2), .Q(out_3[6]));  // open: reset, Qn, preset
  Demultiplexer demultiplexer_8 (.out0(demultiplexer_8_out0), .out1(demultiplexer_8_out1), .in(1'b1), .sel(in_1[7]));
  S_R_Flip_Flop s_r_ff_8 (
    .S(demultiplexer_8_out1), .R(demultiplexer_8_out0), .clk(in_2), .Q(out_3[7]));  // open: reset, Qn, preset
endmodule

module mainMemo (
  input  [7:0] Value,
  input  [1:0] Adress,
  input  Write,
  input  Beginn,
  input  Stopp,
  output [7:0] out_6
);

  wire and_1_out, clock_1_out, demultiplexer_2_out0, demultiplexer_2_out1, demultiplexer_2_out2,
       demultiplexer_2_out3, j_k_ff_1_q, j_k_ff_1_qn, or_1_out, s_r_ff_1_q, s_r_ff_2_qn;
  wire [1:0] not_1_out;
  wire [7:0] demultiplexer_1_out0, demultiplexer_1_out1, demultiplexer_1_out2, demultiplexer_1_out3,
       memory_1_out_3, memory_2_out_3, memory_3_out_3, memory_4_out_3;

  Demultiplexer #(.select(2), .width(8)) demultiplexer_1 (
    .out0(demultiplexer_1_out0), .out1(demultiplexer_1_out1), .out2(demultiplexer_1_out2),
    .out3(demultiplexer_1_out3), .in(Value), .sel(Adress));
  Demultiplexer #(.select(2)) demultiplexer_2 (
    .out0(demultiplexer_2_out0), .out1(demultiplexer_2_out1), .out2(demultiplexer_2_out2),
    .out3(demultiplexer_2_out3), .in(Write), .sel(Adress));
  or or_1 (or_1_out, Beginn, Write);
  memory memory_1 (.in_1(demultiplexer_1_out0), .in_2(demultiplexer_2_out0), .out_3(memory_1_out_3));
  memory memory_2 (.in_1(demultiplexer_1_out1), .in_2(demultiplexer_2_out1), .out_3(memory_2_out_3));
  memory memory_3 (.in_1(demultiplexer_1_out2), .in_2(demultiplexer_2_out2), .out_3(memory_3_out_3));
  memory memory_4 (.in_1(demultiplexer_1_out3), .in_2(demultiplexer_2_out3), .out_3(memory_4_out_3));
  S_R_Flip_Flop s_r_ff_1 (.S(1'b0), .R(1'b0), .clk(1'b0), .Q(s_r_ff_1_q), .reset(Stopp), .preset(Beginn));  // open: Qn
  S_R_Flip_Flop s_r_ff_2 (
    .S(1'b0), .R(1'b0), .clk(1'b0), .reset(or_1_out), .Qn(s_r_ff_2_qn), .preset(Stopp));  // open: Q
  Multiplexer #(.enable("true"), .select(2), .width(8)) multiplexer_1 (
    .in0(memory_1_out_3), .in1(memory_2_out_3), .in2(memory_3_out_3), .in3(memory_4_out_3), .out(out_6),
    .sel(not_1_out), .en(and_1_out));
  Clock clock_1 (.out(clock_1_out));
  and and_1 (and_1_out, s_r_ff_1_q, s_r_ff_2_qn);
  J_K_Flip_Flop j_k_ff_1 (
    .J(s_r_ff_1_q), .K(s_r_ff_1_q), .clk(clock_1_out), .Q(j_k_ff_1_q), .Qn(j_k_ff_1_qn), .preset(Beginn));  // open: reset
  not not_1 (not_1_out[0], j_k_ff_1_qn);
  J_K_Flip_Flop j_k_ff_2 (
    .J(s_r_ff_1_q), .K(s_r_ff_1_q), .clk(j_k_ff_1_q), .Q(not_1_out[1]), .preset(Beginn));  // open: Qn, reset
endmodule
