// Logisim project game.circ as structural Verilog: 6 circuits, main circuit main
module main (
  input  [3:0] in_1,
  input  [3:0] in_2,
  input  [3:0] in_3,
  input  [3:0] in_4
);

  wire [3:0] transpose_1_out_5, transpose_1_out_6, transpose_1_out_7, transpose_1_out_8;
  wire [4:0] joystick_1_x, joystick_1_y;
  wire [5:0] X, Y;
  wire [63:0] addition_1_o0, addition_1_o1, addition_1_o2, addition_1_o3, addition_1_o4, addition_1_o5,
       addition_1_o6, addition_1_o7, addition_1_o8, addition_1_o9, addition_1_o10, addition_1_o11,
       addition_1_o12, addition_1_o13, addition_1_o14, addition_1_o15, addition_1_o16, addition_1_o17,
       addition_1_o18, addition_1_o19, addition_1_o20, addition_1_o21, addition_1_o22, addition_1_o23,
       addition_1_o24, addition_1_o25, addition_1_o26, addition_1_o27, addition_1_o28, addition_1_o29,
       addition_1_o30, addition_1_o31, addition_1_o32, addition_1_o33, addition_1_o34, addition_1_o35,
       addition_1_o36, addition_1_o37, addition_1_o38, addition_1_o39, addition_1_o40, addition_1_o41,
       addition_1_o42, addition_1_o43, addition_1_o44, addition_1_o45, addition_1_o46, addition_1_o47,
       addition_1_o48, addition_1_o49, addition_1_o50, addition_1_o51, addition_1_o52, addition_1_o53,
       addition_1_o54, addition_1_o55, addition_1_o56, addition_1_o57, addition_1_o58, addition_1_o59,
       addition_1_o60, addition_1_o61, addition_1_o62, addition_1_o63;

  transpose transpose_1 (
    .in_1(in_2), .in_2(in_3), .in_3(in_4), .in_4(in_1), .out_5(transpose_1_out_5), .out_6(transpose_1_out_6),
    .out_7(transpose_1_out_7), .out_8(transpose_1_out_8));
  // Probe on joystick_1_x
  Joystick #(.bits(5)) joystick_1 (.x(joystick_1_x), .y(joystick_1_y));
  // Probe on joystick_1_y
  // Probe on X
  coordinateJoystick coordinatejoystick_1 (.in_1(joystick_1_x), .out_2(X));
  coordinateJoystick coordinatejoystick_2 (.in_1(joystick_1_y), .out_2(Y));
  // Probe on Y
  DotMatrix #(.matrixcols(64), .matrixrows(64)) dotmatrix_1 (
    .col0(addition_1_o0), .col1(addition_1_o1), .col2(addition_1_o2), .col3(addition_1_o3),
    .col4(addition_1_o4), .col5(addition_1_o5), .col6(addition_1_o6), .col7(addition_1_o7),
    .col8(addition_1_o8), .col9(addition_1_o9), .col10(addition_1_o10), .col11(addition_1_o11),
    .col12(addition_1_o12), .col13(addition_1_o13), .col14(addition_1_o14), .col15(addition_1_o15),
    .col16(addition_1_o16), .col17(addition_1_o17), .col18(addition_1_o18), .col19(addition_1_o19),
    .col20(addition_1_o20), .col21(addition_1_o21), .col22(addition_1_o22), .col23(addition_1_o23),
    .col24(addition_1_o24), .col25(addition_1_o25), .col26(addition_1_o26), .col27(addition_1_o27),
    .col28(addition_1_o28), .col29(addition_1_o29), .col30(addition_1_o30), .col31(addition_1_o31),
    .col32(addition_1_o32), .col33(addition_1_o33), .col34(addition_1_o34), .col35(addition_1_o35),
    .col36(addition_1_o36), .col37(addition_1_o37), .col38(addition_1_o38), .col39(addition_1_o39),
    .col40(addition_1_o40), .col41(addition_1_o41), .col42(addition_1_o42), .col43(addition_1_o43),
    .col44(addition_1_o44), .col45(addition_1_o45), .col46(addition_1_o46), .col47(addition_1_o47),
    .col48(addition_1_o48), .col49(addition_1_o49), .col50(addition_1_o50), .col51(addition_1_o51),
    .col52(addition_1_o52), .col53(addition_1_o53), .col54(addition_1_o54), .col55(addition_1_o55),
    .col56(addition_1_o56), .col57(addition_1_o57), .col58(addition_1_o58), .col59(addition_1_o59),
    .col60(addition_1_o60), .col61(addition_1_o61), .col62(addition_1_o62), .col63(addition_1_o63));
  Addition addition_1 (
    .R1(transpose_1_out_6), .R2(transpose_1_out_7), .R3(transpose_1_out_8), .R0(transpose_1_out_5), .x(X),
    .y(Y), .o34(addition_1_o34), .o42(addition_1_o42), .o18(addition_1_o18), .o26(addition_1_o26),
    .o50(addition_1_o50), .o58(addition_1_o58), .o2(addition_1_o2), .o10(addition_1_o10),
    .o35(addition_1_o35), .o43(addition_1_o43), .o19(addition_1_o19), .o27(addition_1_o27),
    .o51(addition_1_o51), .o59(addition_1_o59), .o3(addition_1_o3), .o11(addition_1_o11),
    .o36(addition_1_o36), .o44(addition_1_o44), .o20(addition_1_o20), .o28(addition_1_o28),
    .o52(addition_1_o52), .o60(addition_1_o60), .o4(addition_1_o4), .o12(addition_1_o12),
    .o37(addition_1_o37), .o45(addition_1_o45), .o21(addition_1_o21), .o29(addition_1_o29),
    .o53(addition_1_o53), .o61(addition_1_o61), .o5(addition_1_o5), .o13(addition_1_o13),
    .o38(addition_1_o38), .o46(addition_1_o46), .o22(addition_1_o22), .o30(addition_1_o30),
    .o54(addition_1_o54), .o62(addition_1_o62), .o6(addition_1_o6), .o14(addition_1_o14),
    .o39(addition_1_o39), .o47(addition_1_o47), .o23(addition_1_o23), .o31(addition_1_o31),
    .o55(addition_1_o55), .o63(addition_1_o63), .o7(addition_1_o7), .o15(addition_1_o15),
    .o32(addition_1_o32), .o40(addition_1_o40), .o16(addition_1_o16), .o24(addition_1_o24),
    .o48(addition_1_o48), .o56(addition_1_o56), .o0(addition_1_o0), .o8(addition_1_o8), .o33(addition_1_o33),
    .o41(addition_1_o41), .o17(addition_1_o17), .o25(addition_1_o25), .o49(addition_1_o49),
    .o57(addition_1_o57), .o1(addition_1_o1), .o9(addition_1_o9));
endmodule

module speedControl (
  input  [4:0] in_1,
  output out_2
);

  wire clock_1_out, clock_2_out, clock_3_out, clock_4_out, clock_5_out, clock_6_out, clock_7_out,
       clock_8_out, clock_9_out, clock_10_out, clock_11_out, clock_12_out, clock_13_out, clock_14_out,
       clock_15_out, comparator_1_gt;
  wire [4:0] multiplexer_1_out, negator_1_out, subtractor_1_out;

  Subtractor #(.width(5)) subtractor_1 (.a(in_1), .b(5'b10000), .out(subtractor_1_out));  // open: bin, bout
  Comparator #(.width(5)) comparator_1 (.a(subtractor_1_out), .b({5{1'b0}}), .gt(comparator_1_gt));  // open: eq, lt
  Negator #(.width(5)) negator_1 (.in(subtractor_1_out), .out(negator_1_out));
  Multiplexer #(.width(5)) multiplexer_1 (
    .in0(negator_1_out), .in1(subtractor_1_out), .out(multiplexer_1_out), .sel(comparator_1_gt));
  Clock #(.highDuration(10), .lowDuration(10)) clock_1 (.out(clock_1_out));
  Clock #(.highDuration(9), .lowDuration(9)) clock_2 (.out(clock_2_out));
  Clock #(.highDuration(8), .lowDuration(8)) clock_3 (.out(clock_3_out));
  Clock #(.highDuration(7), .lowDuration(7)) clock_4 (.out(clock_4_out));
  Clock #(.highDuration(6), .lowDuration(6)) clock_5 (.out(clock_5_out));
  Clock #(.highDuration(5), .lowDuration(5)) clock_6 (.out(clock_6_out));
  Clock #(.highDuration(4), .lowDuration(4)) clock_7 (.out(clock_7_out));
  Clock #(.highDuration(3), .lowDuration(3)) clock_8 (.out(clock_8_out));
  Clock #(.highDuration(2), .lowDuration(2)) clock_9 (.out(clock_9_out));
  Clock clock_10 (.out(clock_10_out));
  Clock #(.highDuration(12), .lowDuration(12)) clock_11 (.out(clock_11_out));
  Clock #(.highDuration(11), .lowDuration(11)) clock_12 (.out(clock_12_out));
  Clock #(.highDuration(14), .lowDuration(14)) clock_13 (.out(clock_13_out));
  Clock #(.highDuration(13), .lowDuration(13)) clock_14 (.out(clock_14_out));
  Clock #(.highDuration(15), .lowDuration(15)) clock_15 (.out(clock_15_out));
  Multiplexer #(.select(4)) multiplexer_2 (
    .in0(1'b0), .in1(clock_15_out), .in2(clock_13_out), .in3(clock_14_out), .in4(clock_11_out),
    .in5(clock_12_out), .in6(clock_1_out), .in7(clock_2_out), .in8(clock_3_out), .in9(clock_4_out),
    .in10(clock_5_out), .in11(clock_6_out), .in12(clock_7_out), .in13(clock_8_out), .in14(clock_9_out),
    .in15(clock_10_out), .out(out_2), .sel(multiplexer_1_out[3:0]));
endmodule

module coordinateJoystick (
  input  [4:0] in_1,
  output [5:0] out_2
);

  wire comparator_1_lt, speedcontrol_1_out_2;
  wire [5:0] adder_1_out, multiplexer_1_out, subtractor_1_out;

  Comparator #(.mode("unsigned"), .width(5)) comparator_1 (
    .a(in_1), .b(5'b10000), .lt(comparator_1_lt));  // open: gt, eq
  Adder #(.width(6)) adder_1 (.a(out_2), .b(6'b000001), .out(adder_1_out));  // open: cin, cout
  Subtractor #(.width(6)) subtractor_1 (.a(out_2), .b(6'b000001), .out(subtractor_1_out));  // open: bin, bout
  speedControl speedcontrol_1 (.in_1(in_1), .out_2(speedcontrol_1_out_2));
  Multiplexer #(.width(6)) multiplexer_1 (
    .in0(adder_1_out), .in1(subtractor_1_out), .out(multiplexer_1_out), .sel(comparator_1_lt));
  D_Flip_Flop d_ff_1 (.D(multiplexer_1_out[0]), .clk(speedcontrol_1_out_2), .Q(out_2[0]));  // open: Qn, preset, reset
  D_Flip_Flop d_ff_2 (.D(multiplexer_1_out[1]), .clk(speedcontrol_1_out_2), .Q(out_2[1]));  // open: Qn, preset, reset
  D_Flip_Flop d_ff_3 (.D(multiplexer_1_out[2]), .clk(speedcontrol_1_out_2), .Q(out_2[2]));  // open: Qn, preset, reset
  D_Flip_Flop d_ff_4 (.D(multiplexer_1_out[3]), .clk(speedcontrol_1_out_2), .Q(out_2[3]));  // open: Qn, preset, reset
  D_Flip_Flop d_ff_5 (.D(multiplexer_1_out[4]), .clk(speedcontrol_1_out_2), .Q(out_2[4]));  // open: Qn, preset, reset
  D_Flip_Flop d_ff_6 (.D(multiplexer_1_out[5]), .clk(speedcontrol_1_out_2), .Q(out_2[5]));  // open: Qn, preset, reset
endmodule

module objectMove (
  input  [3:0] r0,
  input  [3:0] r1,
  input  [3:0] r2,
  input  [3:0] r3,
  input  [5:0] x,
  input  [5:0] y0,
  input  [5:0] column,
  output [63:0] out_8
);

  wire [3:0] comparator_4_eq;
  wire [5:0] y1, y2, y3;
  wire [63:0] bit_extender_1_out, bit_extender_2_out, bit_extender_3_out, bit_extender_4_out,
       multiplexer_1_out;

  assign bit_extender_1_out = {{60{1'b0}}, r0};  // Bit_Extender bit_extender_1
  assign bit_extender_2_out = {{60{1'b0}}, r1};  // Bit_Extender bit_extender_2
  assign bit_extender_3_out = {{60{1'b0}}, r2};  // Bit_Extender bit_extender_3
  assign bit_extender_4_out = {{60{1'b0}}, r3};  // Bit_Extender bit_extender_4
  Comparator #(.width(6)) comparator_1 (.a(y1), .b(column), .eq(comparator_4_eq[1]));  // open: gt, lt
  Comparator #(.width(6)) comparator_2 (.a(y2), .b(column), .eq(comparator_4_eq[2]));  // open: gt, lt
  Comparator #(.width(6)) comparator_3 (.a(y3), .b(column), .eq(comparator_4_eq[3]));  // open: gt, lt
  Multiplexer #(.select(4), .width(64)) multiplexer_1 (
    .in0({64{1'b0}}), .in1(bit_extender_1_out), .in2(bit_extender_2_out), .in3({64{1'b0}}),
    .in4(bit_extender_3_out), .in5({64{1'b0}}), .in6({64{1'b0}}), .in7({64{1'b0}}), .in8(bit_extender_4_out),
    .in9({64{1'b0}}), .in10({64{1'b0}}), .in11({64{1'b0}}), .in12({64{1'b0}}), .in13({64{1'b0}}),
    .in14({64{1'b0}}), .in15({64{1'b0}}), .out(multiplexer_1_out), .sel(comparator_4_eq));
  // Probe on comparator_4_eq
  Comparator #(.width(6)) comparator_4 (.a(y0), .b(column), .eq(comparator_4_eq[0]));  // open: gt, lt
  Shifter #(.shift("rr"), .width(64)) shifter_1 (.in(multiplexer_1_out), .\dist (x), .out(out_8));
  Adder #(.width(6)) adder_1 (.a(y0), .b(6'b000001), .out(y1));  // open: cin, cout
  Adder #(.width(6)) adder_2 (.a(y1), .b(6'b000001), .out(y2));  // open: cin, cout
  Adder #(.width(6)) adder_3 (.a(y2), .b(6'b000001), .out(y3));  // open: cin, cout
endmodule

module Addition (
  input  [3:0] R0,
  input  [5:0] x,
  input  [3:0] R1,
  input  [3:0] R2,
  input  [3:0] R3,
  input  [5:0] y,
  output [63:0] o0,
  output [63:0] o1,
  output [63:0] o3,
  output [63:0] o4,
  output [63:0] o5,
  output [63:0] o7,
  output [63:0] o2,
  output [63:0] o6,
  output [63:0] o8,
  output [63:0] o9,
  output [63:0] o11,
  output [63:0] o12,
  output [63:0] o13,
  output [63:0] o15,
  output [63:0] o10,
  output [63:0] o14,
  output [63:0] o16,
  output [63:0] o17,
  output [63:0] o19,
  output [63:0] o20,
  output [63:0] o21,
  output [63:0] o23,
  output [63:0] o18,
  output [63:0] o22,
  output [63:0] o24,
  output [63:0] o25,
  output [63:0] o27,
  output [63:0] o28,
  output [63:0] o29,
  output [63:0] o31,
  output [63:0] o26,
  output [63:0] o30,
  output [63:0] o32,
  output [63:0] o33,
  output [63:0] o35,
  output [63:0] o36,
  output [63:0] o37,
  output [63:0] o39,
  output [63:0] o34,
  output [63:0] o38,
  output [63:0] o40,
  output [63:0] o41,
  output [63:0] o43,
  output [63:0] o44,
  output [63:0] o45,
  output [63:0] o47,
  output [63:0] o42,
  output [63:0] o46,
  output [63:0] o48,
  output [63:0] o49,
  output [63:0] o51,
  output [63:0] o52,
  output [63:0] o53,
  output [63:0] o55,
  output [63:0] o50,
  output [63:0] o54,
  output [63:0] o56,
  output [63:0] o57,
  output [63:0] o59,
  output [63:0] o60,
  output [63:0] o61,
  output [63:0] o63,
  output [63:0] o58,
  output [63:0] o62
);

  objectMove objectmove_1 (.r0(R0), .r1(R1), .r2(R2), .r3(R3), .x(x), .y0(y), .column({6{1'b0}}), .out_8(o0));
  objectMove objectmove_2 (.r0(R0), .r1(R1), .r2(R2), .r3(R3), .x(x), .y0(y), .column(6'b001000), .out_8(o8));
  objectMove objectmove_3 (.r0(R0), .r1(R1), .r2(R2), .r3(R3), .x(x), .y0(y), .column(6'b010000), .out_8(o16));
  objectMove objectmove_4 (.r0(R0), .r1(R1), .r2(R2), .r3(R3), .x(x), .y0(y), .column(6'b011000), .out_8(o24));
  objectMove objectmove_5 (.r0(R0), .r1(R1), .r2(R2), .r3(R3), .x(x), .y0(y), .column(6'b100000), .out_8(o32));
  objectMove objectmove_6 (.r0(R0), .r1(R1), .r2(R2), .r3(R3), .x(x), .y0(y), .column(6'b101000), .out_8(o40));
  objectMove objectmove_7 (.r0(R0), .r1(R1), .r2(R2), .r3(R3), .x(x), .y0(y), .column(6'b110000), .out_8(o48));
  objectMove objectmove_8 (.r0(R0), .r1(R1), .r2(R2), .r3(R3), .x(x), .y0(y), .column(6'b111000), .out_8(o56));
  objectMove objectmove_9 (.r0(R0), .r1(R1), .r2(R2), .r3(R3), .x(x), .y0(y), .column(6'b000001), .out_8(o1));
  objectMove objectmove_10 (.r0(R0), .r1(R1), .r2(R2), .r3(R3), .x(x), .y0(y), .column(6'b001001), .out_8(o9));
  objectMove objectmove_11 (.r0(R0), .r1(R1), .r2(R2), .r3(R3), .x(x), .y0(y), .column(6'b010001), .out_8(o17));
  objectMove objectmove_12 (.r0(R0), .r1(R1), .r2(R2), .r3(R3), .x(x), .y0(y), .column(6'b011001), .out_8(o25));
  objectMove objectmove_13 (.r0(R0), .r1(R1), .r2(R2), .r3(R3), .x(x), .y0(y), .column(6'b100001), .out_8(o33));
  objectMove objectmove_14 (.r0(R0), .r1(R1), .r2(R2), .r3(R3), .x(x), .y0(y), .column(6'b101001), .out_8(o41));
  objectMove objectmove_15 (.r0(R0), .r1(R1), .r2(R2), .r3(R3), .x(x), .y0(y), .column(6'b110001), .out_8(o49));
  objectMove objectmove_16 (.r0(R0), .r1(R1), .r2(R2), .r3(R3), .x(x), .y0(y), .column(6'b111001), .out_8(o57));
  objectMove objectmove_17 (.r0(R0), .r1(R1), .r2(R2), .r3(R3), .x(x), .y0(y), .column(6'b000010), .out_8(o2));
  objectMove objectmove_18 (.r0(R0), .r1(R1), .r2(R2), .r3(R3), .x(x), .y0(y), .column(6'b001010), .out_8(o10));
  objectMove objectmove_19 (.r0(R0), .r1(R1), .r2(R2), .r3(R3), .x(x), .y0(y), .column(6'b010010), .out_8(o18));
  objectMove objectmove_20 (.r0(R0), .r1(R1), .r2(R2), .r3(R3), .x(x), .y0(y), .column(6'b011010), .out_8(o26));
  objectMove objectmove_21 (.r0(R0), .r1(R1), .r2(R2), .r3(R3), .x(x), .y0(y), .column(6'b100010), .out_8(o34));
  objectMove objectmove_22 (.r0(R0), .r1(R1), .r2(R2), .r3(R3), .x(x), .y0(y), .column(6'b101010), .out_8(o42));
  objectMove objectmove_23 (.r0(R0), .r1(R1), .r2(R2), .r3(R3), .x(x), .y0(y), .column(6'b110010), .out_8(o50));
  objectMove objectmove_24 (.r0(R0), .r1(R1), .r2(R2), .r3(R3), .x(x), .y0(y), .column(6'b111010), .out_8(o58));
  objectMove objectmove_25 (.r0(R0), .r1(R1), .r2(R2), .r3(R3), .x(x), .y0(y), .column(6'b000011), .out_8(o3));
  objectMove objectmove_26 (.r0(R0), .r1(R1), .r2(R2), .r3(R3), .x(x), .y0(y), .column(6'b001011), .out_8(o11));
  objectMove objectmove_27 (.r0(R0), .r1(R1), .r2(R2), .r3(R3), .x(x), .y0(y), .column(6'b010011), .out_8(o19));
  objectMove objectmove_28 (.r0(R0), .r1(R1), .r2(R2), .r3(R3), .x(x), .y0(y), .column(6'b011011), .out_8(o27));
  objectMove objectmove_29 (.r0(R0), .r1(R1), .r2(R2), .r3(R3), .x(x), .y0(y), .column(6'b100011), .out_8(o35));
  objectMove objectmove_30 (.r0(R0), .r1(R1), .r2(R2), .r3(R3), .x(x), .y0(y), .column(6'b101011), .out_8(o43));
  objectMove objectmove_31 (.r0(R0), .r1(R1), .r2(R2), .r3(R3), .x(x), .y0(y), .column(6'b110011), .out_8(o51));
  objectMove objectmove_32 (.r0(R0), .r1(R1), .r2(R2), .r3(R3), .x(x), .y0(y), .column(6'b111011), .out_8(o59));
  objectMove objectmove_33 (.r0(R0), .r1(R1), .r2(R2), .r3(R3), .x(x), .y0(y), .column(6'b000100), .out_8(o4));
  objectMove objectmove_34 (.r0(R0), .r1(R1), .r2(R2), .r3(R3), .x(x), .y0(y), .column(6'b001100), .out_8(o12));
  objectMove objectmove_35 (.r0(R0), .r1(R1), .r2(R2), .r3(R3), .x(x), .y0(y), .column(6'b010100), .out_8(o20));
  objectMove objectmove_36 (.r0(R0), .r1(R1), .r2(R2), .r3(R3), .x(x), .y0(y), .column(6'b011100), .out_8(o28));
  objectMove objectmove_37 (.r0(R0), .r1(R1), .r2(R2), .r3(R3), .x(x), .y0(y), .column(6'b100100), .out_8(o36));
  objectMove objectmove_38 (.r0(R0), .r1(R1), .r2(R2), .r3(R3), .x(x), .y0(y), .column(6'b101100), .out_8(o44));
  objectMove objectmove_39 (.r0(R0), .r1(R1), .r2(R2), .r3(R3), .x(x), .y0(y), .column(6'b110100), .out_8(o52));
  objectMove objectmove_40 (.r0(R0), .r1(R1), .r2(R2), .r3(R3), .x(x), .y0(y), .column(6'b111100), .out_8(o60));
  objectMove objectmove_41 (.r0(R0), .r1(R1), .r2(R2), .r3(R3), .x(x), .y0(y), .column(6'b000101), .out_8(o5));
  objectMove objectmove_42 (.r0(R0), .r1(R1), .r2(R2), .r3(R3), .x(x), .y0(y), .column(6'b001101), .out_8(o13));
  objectMove objectmove_43 (.r0(R0), .r1(R1), .r2(R2), .r3(R3), .x(x), .y0(y), .column(6'b010101), .out_8(o21));
  objectMove objectmove_44 (.r0(R0), .r1(R1), .r2(R2), .r3(R3), .x(x), .y0(y), .column(6'b011101), .out_8(o29));
  objectMove objectmove_45 (.r0(R0), .r1(R1), .r2(R2), .r3(R3), .x(x), .y0(y), .column(6'b100101), .out_8(o37));
  objectMove objectmove_46 (.r0(R0), .r1(R1), .r2(R2), .r3(R3), .x(x), .y0(y), .column(6'b101101), .out_8(o45));
  objectMove objectmove_47 (.r0(R0), .r1(R1), .r2(R2), .r3(R3), .x(x), .y0(y), .column(6'b110101), .out_8(o53));
  objectMove objectmove_48 (.r0(R0), .r1(R1), .r2(R2), .r3(R3), .x(x), .y0(y), .column(6'b111101), .out_8(o61));
  objectMove objectmove_49 (.r0(R0), .r1(R1), .r2(R2), .r3(R3), .x(x), .y0(y), .column(6'b000110), .out_8(o6));
  objectMove objectmove_50 (.r0(R0), .r1(R1), .r2(R2), .r3(R3), .x(x), .y0(y), .column(6'b001110), .out_8(o14));
  objectMove objectmove_51 (.r0(R0), .r1(R1), .r2(R2), .r3(R3), .x(x), .y0(y), .column(6'b010110), .out_8(o22));
  objectMove objectmove_52 (.r0(R0), .r1(R1), .r2(R2), .r3(R3), .x(x), .y0(y), .column(6'b011110), .out_8(o30));
  objectMove objectmove_53 (.r0(R0), .r1(R1), .r2(R2), .r3(R3), .x(x), .y0(y), .column(6'b100110), .out_8(o38));
  objectMove objectmove_54 (.r0(R0), .r1(R1), .r2(R2), .r3(R3), .x(x), .y0(y), .column(6'b101110), .out_8(o46));
  objectMove objectmove_55 (.r0(R0), .r1(R1), .r2(R2), .r3(R3), .x(x), .y0(y), .column(6'b110110), .out_8(o54));
  objectMove objectmove_56 (.r0(R0), .r1(R1), .r2(R2), .r3(R3), .x(x), .y0(y), .column(6'b111110), .out_8(o62));
  objectMove objectmove_57 (.r0(R0), .r1(R1), .r2(R2), .r3(R3), .x(x), .y0(y), .column(6'b000111), .out_8(o7));
  objectMove objectmove_58 (.r0(R0), .r1(R1), .r2(R2), .r3(R3), .x(x), .y0(y), .column(6'b001111), .out_8(o15));
  objectMove objectmove_59 (.r0(R0), .r1(R1), .r2(R2), .r3(R3), .x(x), .y0(y), .column(6'b010111), .out_8(o23));
  objectMove objectmove_60 (.r0(R0), .r1(R1), .r2(R2), .r3(R3), .x(x), .y0(y), .column(6'b011111), .out_8(o31));
  objectMove objectmove_61 (.r0(R0), .r1(R1), .r2(R2), .r3(R3), .x(x), .y0(y), .column(6'b100111), .out_8(o39));
  objectMove objectmove_62 (.r0(R0), .r1(R1), .r2(R2), .r3(R3), .x(x), .y0(y), .column(6'b101111), .out_8(o47));
  objectMove objectmove_63 (.r0(R0), .r1(R1), .r2(R2), .r3(R3), .x(x), .y0(y), .column(6'b110111), .out_8(o55));
  objectMove objectmove_64 (.r0(R0), .r1(R1), .r2(R2), .r3(R3), .x(x), .y0(y), .column({6{1'b1}}), .out_8(o63));

  // Other names for the same wires on the sheet: r1_t[3:0] = R0; r2_t[3:0] = R1; r3_t[3:0] = R2; r4[3:0] = R3;
  //   xx[5:0] = x; yy[5:0] = y
endmodule

module transpose (
  input  [3:0] in_1,
  input  [3:0] in_2,
  input  [3:0] in_3,
  input  [3:0] in_4,
  output [3:0] out_5,
  output [3:0] out_6,
  output [3:0] out_7,
  output [3:0] out_8
);


  assign out_5 = {in_4[3], in_3[3], in_2[3], in_1[3]};
  assign out_6 = {in_4[2], in_3[2], in_2[2], in_1[2]};
  assign out_7 = {in_4[1], in_3[1], in_2[1], in_1[1]};
  assign out_8 = {in_4[0], in_3[0], in_2[0], in_1[0]};
endmodule
