// Logisim project timer.circ as structural Verilog: 5 circuits, main circuit main
module main (
  input  [7:0] in_1,
  input  [7:0] in_2,
  input  [7:0] in_3,
  input  in_4,
  input  in_5,
  input  in_6,
  input  in_7,
  output [7:0] out_8,
  output out_9,
  output out_10,
  output out_11,
  output out_12,
  output out_13
);

  wire clock_1_out;

  Clock clock_1 (.out(clock_1_out));
  timerHelper timerhelper_1 (
    .presc(in_1), .clc(clock_1_out), .OCA(in_2), .OCB(in_3), .OCAIE(in_4), .OCBIE(in_5), .OIE(in_6),
    .WGM(in_7), .counterReg(out_8), .IFOCA(out_9), .IFOCB(out_10), .IFO(out_11), .WGMO(out_12),
    .interrupted(out_13));
endmodule

module prescaler (
  input  [7:0] info,
  input  clc,
  output presc
);

  wire comparator_1_eq, comparator_1_gt, comparator_2_eq, d_ff_1_q, or_1_out;
  wire [7:0] counter_1_q, subtractor_1_out;

  Comparator #(.mode("unsigned")) comparator_1 (
    .a(info), .b(8'h2), .gt(comparator_1_gt), .eq(comparator_1_eq));  // open: lt
  or or_1 (or_1_out, comparator_1_gt, comparator_1_eq);
  Counter counter_1 (.count(clc), .Q(counter_1_q), .up(1'b1), .clk(clc), .clr(presc));  // open: load, D, carry
  Multiplexer multiplexer_1 (.in0(clc), .in1(d_ff_1_q), .out(presc), .sel(or_1_out));
  Subtractor subtractor_1 (.a(info), .b(counter_1_q), .out(subtractor_1_out));  // open: bin, bout
  Comparator #(.mode("unsigned")) comparator_2 (.a(subtractor_1_out), .b(8'h2), .eq(comparator_2_eq));  // open: gt, lt
  D_Flip_Flop d_ff_1 (.D(comparator_2_eq), .clk(clc), .Q(d_ff_1_q));  // open: Qn, preset, reset
endmodule

module timerHelper (
  input  [7:0] presc,
  input  clc,
  input  [7:0] OCA,
  input  [7:0] OCB,
  input  OCAIE,
  input  OCBIE,
  input  OIE,
  input  WGM,
  output [7:0] counterReg,
  output IFOCA,
  output IFOCB,
  output IFO,
  output WGMO,
  output interrupted
);

  wire oie_t, scaledclck;

  prescaler prescaler_1 (.info(presc), .clc(clc), .presc(scaledclck));
  Counter counter_1 (.Q(counterReg), .carry(oie_t), .clk(scaledclck));  // open: load, D, count, up, clr
  or or_1 (interrupted, IFOCA, IFOCB);
  helper helper_1 (.OCAB(OCA), .count(counterReg), .OCABIE(OCAIE), .IFOCAB(IFOCA));
  helper helper_2 (.OCAB(OCB), .count(counterReg), .OCABIE(OCBIE), .IFOCAB(IFOCB));
  helper helper_3 (.OCAB({8{1'b1}}), .count(counterReg), .OCABIE(OIE), .IFOCAB(IFO));
  waveformHelper waveformhelper_1 (.IFOCA(IFOCA), .IFOCB(IFOCB), .WGM(WGM), .WGMO(WGMO));

  // Other names for the same wires on the sheet: cntr[7:0] = counterReg
endmodule

module helper (
  input  [7:0] OCAB,
  input  [7:0] count,
  input  OCABIE,
  output IFOCAB
);

  wire comparator_1_eq, comparator_1_lt, comparator_2_gt, or_1_out, or_2_out, out1, out2;
  wire [7:0] adder_1_out, divider_1_rem;

  Divider divider_1 (.a(OCAB), .b({8{1'b1}}), .rem(divider_1_rem));  // open: out, upper
  Adder adder_1 (.a(divider_1_rem), .b(8'h3), .out(adder_1_out));  // open: cin, cout
  Comparator comparator_1 (.a(OCAB), .b(count), .eq(comparator_1_eq), .lt(comparator_1_lt));  // open: gt
  Comparator comparator_2 (.a(adder_1_out), .b(count), .gt(comparator_2_gt));  // open: eq, lt
  or or_1 (or_1_out, comparator_1_lt, comparator_1_eq);
  and and_1 (out1, or_1_out, comparator_2_gt);
  or or_2 (or_2_out, out1, out2);
  and and_2 (IFOCAB, or_2_out, OCABIE);
  Comparator comparator_3 (.a(count), .b(OCAB), .eq(out2));  // open: gt, lt
endmodule

module waveformHelper (
  input  IFOCA,
  input  IFOCB,
  input  WGM,
  output WGMO
);

  wire and_1_out, j_k_ff_1_q, or_1_out;

  or or_1 (or_1_out, IFOCA, IFOCB);
  and and_1 (and_1_out, IFOCB, IFOCA);
  J_K_Flip_Flop j_k_ff_1 (.J(IFOCA), .K(IFOCB), .clk(or_1_out), .Q(j_k_ff_1_q), .reset(and_1_out));  // open: Qn, preset
  and and_2 (WGMO, j_k_ff_1_q, WGM);
endmodule
